# Fritzing sketch Huzzah_BME280_Sensor (saved by Fritzing 0.9.3b)

parts:
  Huzzah_Power_Binary_Sensor = Adafruit Feather HUZZAH ESP8266 [part_number="Adafruit #2821"]
  Part1 = BME280 Breakout

nets:
  GND: Huzzah_Power_Binary_Sensor.GND, Part1.GND
  3.3V: Huzzah_Power_Binary_Sensor.3.3V, Part1.3.3V
  N1: Huzzah_Power_Binary_Sensor.GPIO5/SCL, Part1.SCK/SCL
  N2: Huzzah_Power_Binary_Sensor.GPIO4/SDA, Part1.SDI/SDA

custom parts:
  Adafruit Feather HUZZAH ESP8266: his is the Adafruit Feather HUZZAH ESP8266 - our take on an 'all-in-one' ESP8266 WiFi development board with built in USB and battery charging. Its an ESP8266 WiFi module with all the extras you need, ready to rock! We have other boards in the Feather family, check'em out here. At the Feather HUZZAH's heart is an ESP8266 WiFi microcontroller clocked at 80 MHz and at 3.3V logic. This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

// code stored in the sketch: main.ino
void setup() {
  // do your stuff, like setup WiFi
}

void loop() {

    

}
